# Fritzing sketch ColorimetroLedUnoEsp8266 (saved by Fritzing 0.9.3b)
breadboards: 2

parts:
  ESP8266_NodeMCU = ESP8266 NodeMCU LoLin module
  8x8_LED = 8x8 LED Modul mit MAX7219 [package=THT]
  Arduino_UNO = Arduino Uno (Rev3) - ICSP
  Colorímetro = TCS230 Color Sensor [part_number=101209]

nets:
  GND: ESP8266_NodeMCU.GND, 8x8_LED.GND_Eingang, Arduino_UNO.ICSP_MISO, Arduino_UNO.GND, Arduino_UNO.D10_PWM/SS, Arduino_UNO.D12/MISO, Colorímetro.Gnd, Colorímetro.OE, Colorímetro.S3, Colorímetro.Out
  N1: ESP8266_NodeMCU.RX, Arduino_UNO.D1/TX
  N2: ESP8266_NodeMCU.TX, Arduino_UNO.D0/RX
  5V: 8x8_LED.VCC_Eingang, Arduino_UNO.5V, Colorímetro.Vcc
  N3: 8x8_LED.DIN_Eingang, Arduino_UNO.D7
  N4: 8x8_LED.CS_Eingang, Arduino_UNO.D6_PWM
  N5: 8x8_LED.CLK_Eingang, Arduino_UNO.D5_PWM
  N6: Arduino_UNO.D8, Colorímetro.S2
  N7: Arduino_UNO.D9_PWM, Colorímetro.S0
  N8: Arduino_UNO.D11_PWM/MOSI, Colorímetro.S1

notes:
  naranja Tx
  amarillo Rx
  naranja Rx
  amarillo Tx

custom parts:
  ESP8266 NodeMCU LoLin module: ESP8266 based NodeMCU
  TCS230 Color Sensor: TCS230
